// Logisim project Parity using XOR gate.circ as structural Verilog: 1 circuit, main circuit main
module main (
  input  in_1,
  input  in_2,
  input  in_3,
  input  in_4,
  output out_5,
  output out_6
);

  wire xor_1_out, xor_2_out;

  xor xor_1 (xor_1_out, in_1, in_2);
  xor xor_2 (xor_2_out, in_3, in_4);
  xor xor_3 (out_5, xor_1_out, xor_2_out);
  not not_1 (out_6, out_5);
endmodule
